# Fritzing sketch booster_v2 (saved by Fritzing 0.9.2b)
circuit board: 7.01111cm x 5.32294cm
breadboards: 2

parts:
  U1 = LMD1820X [package=to-220-11lead]
  J1 = Power Jack [package=power_jack_pth_lock]
  C1 = Ceramic Capacitor [capacitance=10nF package="100 mil [THT, multilayer]"]
  C2 = Ceramic Capacitor [capacitance=10nF package="100 mil [THT, multilayer]"]
  J2 = Screw terminal - 2 pins [package=THT]
  C3 = Electrolytic Capacitor [capacitance=1mF voltage=35V package="100 mil [THT, electrolytic]"]
  U2 = Voltage Regulator - 5V [package="TO220 [THT]"]
  C5 = Ceramic Capacitor [capacitance=10nF package="100 mil [THT, multilayer]"]
  LED1 = LED - 5mm [color="Green (555nm)" package="5 mm [THT]"]
  JP1 = Header 2 [package=r_sw_th]
  R1 = Resistor [tolerance=±5% resistance=150 package=THT]
  R2 = Resistor [tolerance=±5% resistance=150 package=THT]
  LED2 = LED - 5mm [color="Red (633nm)" package="5 mm [THT]"]
  J3 = RJ11 Jack [package=rj11-6]

nets:
  GND: U1.BS1, U1.OUT1, U1.DIR, U1.BRK, U1.PWM, U1.PWR, U1.PGND, U1.SGND, U1.TF, U1.OUT2, U1.BS2, J1.GND, C1.0, C1.1, C2.0, C2.1, J2.pin1, J2.pin2, C3.-, C3.+, U2.input_voltage, U2.GND, U2.output_voltage, C5.0, C5.1, LED1.cathode, JP1.2, R1.Pin_1, R2.Pin_1, LED2.cathode, J3.3, J3.4, J3.5
  N1: J1.PWR, JP1.1
  N2: LED1.anode, R1.Pin_0
  N3: R2.Pin_0, LED2.anode

notes:
  FreeDCC Booster v0.1
